// Logisim project item_a.circ as structural Verilog: 1 circuit, main circuit circ_a
module circ_a (
  input  A,
  input  B,
  input  C,
  output x
);

  wire and_1_out, not_1_out;

  not not_1 (not_1_out, A);
  and and_1 (and_1_out, not_1_out, B);
  or or_1 (x, and_1_out, C);
endmodule
